# Fritzing sketch pcb_VINDRIKTNING (saved by Fritzing 0.9.4)

parts:
  Componente1 = Logic Level Converter
  WeMos_D1_Mini1 = WeMos D1 Mini
  VINDRIKTNING_Board = Header 6 [part_number="LED_G | R3 | R4 | 5V | GND | REST" package=molex-1x6_lock]
  F1 = Fan - Ventilador [package=THT]
  MH-MINI-360 = RioRand LM2596 [part_number=3v3]
  R1 = PHOTOCELL [part_number=LED_R_1 package=photocell]
  D1 = Diode [package=diode-1n4148]

nets:
  N1: Componente1.TX2_LV, WeMos_D1_Mini1.D5
  N2: Componente1.RX2_LV, WeMos_D1_Mini1.D6
  N3: Componente1.LV, WeMos_D1_Mini1.3V3
  N4: Componente1.RX_LV, WeMos_D1_Mini1.D7
  N5: Componente1.RX_HV, VINDRIKTNING_Board.R3_(RED)
  5V: Componente1.HV, WeMos_D1_Mini1.5V, VINDRIKTNING_Board.5V, MH-MINI-360.Pin_1
  GND: Componente1.GND, WeMos_D1_Mini1.G, VINDRIKTNING_Board.GND, MH-MINI-360.Pin_2
  N6: Componente1.RX2_HV, VINDRIKTNING_Board.R4_(ORANGE)
  N7: Componente1.TX2_HV, VINDRIKTNING_Board.LEG_G
  N8: WeMos_D1_Mini1.A0, R1.P$2
  N9: WeMos_D1_Mini1.D2, VINDRIKTNING_Board.REST
  N10: F1.5V, MH-MINI-360.Pin_3, D1.A
  N11: F1.GND, MH-MINI-360.Pin_4, D1.C

custom parts:
  Header 6: Header 6 Standard 6-pin 0.1 header. Use with straight break away headers (SKU : PRT-00116), right angle break away headers (PRT-00553), swiss pins (PRT-00743), machine pins (PRT-00117), and female headers (PRT-00115). Molex polarized connector foot print use with SKU : PRT-08094 with associated crimp pins and housings. NOTES ON THE VARIANTS LOCK and LOCK_LONGPADS... This footprint was designed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
  Fan - Ventilador: Ventilador de 2 pines, se encuentra comunmente en computadoras de escritorio
